# Fritzing sketch martha-pi (saved by Fritzing 0.9.4)
breadboards: 1

parts:
  Raspberry_Pi1 = Raspberry Pi B+
  RHT2 = Humidity and Temperature Sensor RHT03 [part_number=DHT22]
  KY-2 = Keyes Relay [package=THT]
  KY-3 = Keyes Relay [package=THT]

nets:
  N1: Raspberry_Pi1.GPIO4, RHT2.Data-signal
  N2: Raspberry_Pi1.GND, RHT2.GND_2, KY-2.ground, KY-3.ground
  5V: Raspberry_Pi1.5V, RHT2.Vcc, KY-2.signal, KY-3.signal

custom parts:
  Keyes Relay: The Keyes 5V relay module is suitable for SCM development, home appliance control. It uses a 5V~12V TIL control signal which can control DC / AC signal.
